# Fritzing sketch flarmer (saved by Fritzing 0.9.3b)

parts:
  RHT1 = Humidity and Temperature Sensor RHT03
  Часть1 = Color Sensor Breakout ADJD-S311
  BAT1 = LIPO-1000mAh [package=lipo-1000]
  WeMos_D1_Mini1 = WeMos D1 Mini

nets (from the schematic view):
  VCC: RHT1.Vcc, Часть1.VCC, WeMos_D1_Mini1.3V3
  N1: RHT1.Data-signal, WeMos_D1_Mini1.D3
  N2: RHT1.GND_2, Часть1.GND#7, BAT1.-, WeMos_D1_Mini1.G
  N3: Часть1.SCL, WeMos_D1_Mini1.D1
  N4: Часть1.SDA, WeMos_D1_Mini1.D2
  N5: BAT1.+, WeMos_D1_Mini1.5V
